// Logisim project ATV 2.circ as structural Verilog: 1 circuit, main circuit ATIVIDADE 1 
module ATIVIDADE_1 (
);

  wire and_1_out, and_2_out, and_3_out, nand_1_out, nand_2_out, nand_3_out, not_1_out, not_2_out, not_3_out,
       not_5_out, or_1_out, undriven, undriven_2, undriven_3;

  not not_1 (not_1_out, undriven);
  and and_1 (and_1_out, undriven_3, undriven_2);
  and and_2 (and_2_out, not_1_out, undriven_2);
  not not_2 (not_2_out, undriven_3);
  not not_3 (not_3_out, undriven_2);
  not not_4 (not_2_out, and_2_out);
  nand nand_1 (nand_1_out, not_3_out, and_2_out, and_1_out);
  and and_3 (and_3_out, not_2_out, not_2_out);
  not nand_2 (nand_2_out, not_2_out);  // NAND_Gate
  not not_5 (not_5_out, and_3_out);
  nand nand_3 (nand_3_out, and_3_out, nand_1_out);
  or or_1 (or_1_out, nand_2_out, not_5_out, nand_3_out);

  // Notes on the sheet:
  //   A
  //   C
  //   B
  //   S
endmodule
