// Logisim project CIRCUITO MAPA.circ as structural Verilog: 1 circuit, main circuit main
module main (
);

  wire and_1_out, not_1_out, undriven, undriven_2, undriven_3;

  not not_1 (not_1_out, undriven_3);
  and and_1 (and_1_out, undriven, undriven_2);
  // OR_Gate or_1 has open pins: in1=not_1_out, in3=and_1_out, out=open

  // Notes on the sheet:
  //   B
  //   A
  //   C
  //   S
endmodule
