// Logisim project FORMA NORMAL CIRCUITO 2.circ as structural Verilog: 1 circuit, main circuit main
module main (
);

  wire and_1_out, not_1_out, not_2_out, not_3_out, or_1_out, or_2_out, or_3_out, or_6_out, or_7_out,
       undriven, undriven_2, undriven_3;

  not not_1 (not_1_out, undriven_2);
  not not_2 (not_2_out, undriven);
  not not_3 (not_3_out, undriven_3);
  or or_1 (or_1_out, not_2_out, not_1_out, not_3_out);
  or or_2 (or_2_out, not_2_out, not_1_out, undriven_3);
  or or_3 (or_3_out, not_2_out, undriven_2, not_3_out);
  or or_4 (or_3_out, undriven, not_1_out, not_3_out);
  or or_5 (or_3_out, undriven, not_1_out, undriven_2);
  or or_6 (or_6_out, undriven, undriven_3, not_3_out);
  or or_7 (or_7_out, undriven_3, undriven_2, undriven);
  and and_1 (and_1_out, or_1_out, or_2_out, or_3_out, or_6_out, or_7_out);

  // Notes on the sheet:
  //   A
  //   C
  //   B
  //   S
endmodule
