// Logisim project FORMA NORMAL CIRCUITO.circ as structural Verilog: 1 circuit, main circuit main
module main (
);

  wire and_1_out, not_1_out, not_2_out, not_3_out, not_4_out, not_5_out, not_6_out, not_7_out, not_8_out,
       not_9_out, or_1_out, or_2_out, or_3_out, or_4_out, or_6_out, undriven, undriven_2, undriven_3;

  not not_1 (not_1_out, undriven);
  not not_2 (not_2_out, undriven);
  not not_3 (not_3_out, undriven);
  not not_4 (not_4_out, undriven_2);
  not not_5 (not_5_out, undriven_2);
  not not_6 (not_6_out, undriven_2);
  not not_7 (not_7_out, undriven_2);
  not not_8 (not_8_out, undriven_3);
  not not_9 (not_9_out, undriven_3);
  or or_1 (or_1_out, undriven, undriven_2, undriven_3);
  or or_2 (or_2_out, undriven_3, not_4_out, undriven);
  or or_3 (or_3_out, not_8_out, not_5_out, undriven);
  or or_4 (or_4_out, not_1_out, undriven_2, undriven_3);
  or or_5 (or_2_out, not_2_out, not_6_out, undriven_3);
  or or_6 (or_6_out, not_3_out, not_7_out, not_9_out);
  and and_1 (and_1_out, or_1_out, or_3_out, or_2_out, or_4_out, or_6_out);

  // Notes on the sheet:
  //   B
  //   A
  //   C
  //   S
endmodule
