// Logisim project FORMA NORMAL CONJUTIVA CIRCUITO.circ as structural Verilog: 1 circuit, main circuit main
module main (
);

  wire not_1_out, or_1_out, undriven, undriven_2, undriven_3;

  not not_1 (not_1_out, undriven_2);
  or or_1 (or_1_out, undriven_3, not_1_out, undriven);

  // Notes on the sheet:
  //   A
  //   C
  //   B
  //   S
endmodule
