// Logisim project SOMADOR.circ as structural Verilog: 3 circuits, main circuit main
module main (
  input  B4,
  input  A4,
  input  B3,
  input  A3,
  input  B2,
  input  A2,
  input  B1,
  input  A1,
  input  A0,
  input  B0,
  input  C4,
  input  C3,
  input  C2,
  input  C1,
  input  C0,
  output Ts,
  output AB_4,
  output AB_3,
  output AB_2,
  output AB_1,
  output AB_0,
  output Ts_2,
  output S3,
  output S3_2,
  output S2,
  output S1,
  output S0
);

  wire meio_somador_1_ts, meio_somador_2_ts, somador_completo_3_ts, somador_completo_4_ts,
       somador_completo_5_ts, somador_completo_6_ts, somador_completo_7_ts, somador_completo_8_ts;

  SOMADOR_COMPLETO somador_completo_1 (.A(A4), .B(B4), .Te(somador_completo_3_ts), .S(AB_4), .Ts(Ts));
  SOMADOR_COMPLETO somador_completo_2 (.A(AB_4), .B(C4), .Te(somador_completo_4_ts), .S(S3), .Ts(Ts_2));
  SOMADOR_COMPLETO somador_completo_3 (
    .A(A3), .B(B3), .Te(somador_completo_5_ts), .S(AB_3), .Ts(somador_completo_3_ts));
  SOMADOR_COMPLETO somador_completo_4 (
    .A(AB_3), .B(C3), .Te(somador_completo_6_ts), .S(S3_2), .Ts(somador_completo_4_ts));
  SOMADOR_COMPLETO somador_completo_5 (
    .A(A2), .B(B2), .Te(somador_completo_7_ts), .S(AB_2), .Ts(somador_completo_5_ts));
  SOMADOR_COMPLETO somador_completo_6 (
    .A(AB_2), .B(C2), .Te(somador_completo_8_ts), .S(S2), .Ts(somador_completo_6_ts));
  SOMADOR_COMPLETO somador_completo_7 (.A(A1), .B(B1), .Te(meio_somador_1_ts), .S(AB_1), .Ts(somador_completo_7_ts));
  SOMADOR_COMPLETO somador_completo_8 (.A(AB_1), .B(C1), .Te(meio_somador_2_ts), .S(S1), .Ts(somador_completo_8_ts));
  MEIO_SOMADOR meio_somador_1 (.A(B0), .B(A0), .S(AB_0), .TS(meio_somador_1_ts));
  MEIO_SOMADOR meio_somador_2 (.A(AB_0), .B(C0), .S(S0), .TS(meio_somador_2_ts));

  // Notes on the sheet:
  //   MEIO SOMADOR = MS
  //   SC
  //   SC
  //   SC
  //   SC
  //   SC
  //   SC
  //   OBS: VALORS DE A, B E C SÃO MERAMENTE ILUSTRATIVOS
  //   SOMADOR COMPLETO = SC
  //   SC
  //   SC
  //   MS
  //   MS
endmodule

module MEIO_SOMADOR (
  input  A,
  input  B,
  output S,
  output TS
);

  xor xor_1 (S, A, B);
  and and_1 (TS, A, B);
endmodule

module SOMADOR_COMPLETO (
  input  A,
  input  B,
  input  Te,
  output S,
  output Ts
);

  wire and_1_out, and_2_out, and_3_out, xor_1_out;

  xor xor_1 (xor_1_out, A, B);
  and and_1 (and_1_out, B, Te);
  and and_2 (and_2_out, Te, A);
  and and_3 (and_3_out, B, A);
  xor xor_2 (S, xor_1_out, Te);
  or or_1 (Ts, and_1_out, and_2_out, and_3_out);
endmodule
