// Logisim project Circuito Somador.circ as structural Verilog: 2 circuits, main circuit main
module main (
  input  _1,
  output Q_0,
  output Q_1,
  output Q_2,
  output Q_3,
  output Q_4
);

  wire CK_out, nand_1_out;

  Clock CK (.out(CK_out));
  Flip_Flop_JK___M_E ff_jk_m_e_1 (.J(_1), .C(CK_out), .K(_1), .CLR(nand_1_out), .Q(Q_0));  // open: PR, Q_prime
  Flip_Flop_JK___M_E ff_jk_m_e_2 (.J(_1), .C(Q_0), .K(_1), .CLR(nand_1_out), .Q(Q_1));  // open: PR, Q_prime
  Flip_Flop_JK___M_E ff_jk_m_e_3 (.J(_1), .C(Q_1), .K(_1), .CLR(nand_1_out), .Q(Q_2));  // open: PR, Q_prime
  Flip_Flop_JK___M_E ff_jk_m_e_4 (.J(_1), .C(Q_2), .K(_1), .CLR(nand_1_out), .Q(Q_3));  // open: PR, Q_prime
  Flip_Flop_JK___M_E ff_jk_m_e_5 (.J(_1), .C(Q_3), .K(_1), .CLR(nand_1_out), .Q(Q_4));  // open: PR, Q_prime
  nand nand_1 (nand_1_out, Q_2, Q_0, Q_4);

  // Notes on the sheet:
  //   T0
  //   Q0
  //   CLR
  //   1
  //   CK
  //   CLR
  //   0
  //   T1
  //   Q1
  //   CK
  //   T2
  //   CLR
  //   CONTADOR SEQUENCIAL DE 0 - 20
  //   1
  //   Q2
  //   CK
  //   CLR
  //   T3
  //   Q3
  //   0
  //   T4
  //   CK
  //   CLR
  //   1
  //   Q4
endmodule

module Flip_Flop_JK___M_E (
  input  PR,
  input  J,
  input  C,
  input  K,
  input  CLR,
  output Q,
  output Q_prime
);

  wire nand_1_out, nand_2_out, nand_3_out, nand_4_out, nand_5_out, nand_6_out, not_1_out, undriven,
       undriven_2;

  nand nand_1 (nand_1_out, J, C, Q_prime);
  nand nand_2 (nand_2_out, Q, C, K);
  not not_1 (not_1_out, C);
  nand nand_3 (nand_3_out, undriven, nand_1_out, nand_4_out);
  nand nand_4 (nand_4_out, nand_3_out, nand_2_out, undriven_2);
  nand nand_5 (nand_5_out, nand_3_out, not_1_out);
  nand nand_6 (nand_6_out, not_1_out, nand_4_out);
  nand nand_7 (Q, undriven, nand_5_out, Q_prime);
  nand nand_8 (Q_prime, Q, nand_6_out, undriven_2);
endmodule
